# Fritzing sketch sketch (saved by Fritzing 0.9.5d)

parts:
  Компонент1 = Arduino Uno (Rev3)
  U1 = POT [package=alps_pot]
  U2 = POT [package=alps_pot]
  U3 = POT [package=alps_pot]
  S1 = Pushbutton [package="[SMD]"]
  LED1 = smd LED [color="Red (633nm)" package="0603 [SMD]"]
  R1 = Resistor [tolerance=±5% resistance=220 package="2010 [SMD]"]

nets:
  N1: Компонент1.A0, U1.S
  N2: Компонент1.A1, U2.S
  N3: Компонент1.A2, U3.S
  N4: Компонент1.D8, R1.Pin_0
  N5: Компонент1.GND, LED1.cathode
  N6: Компонент1.D5_PWM, S1.Pin_3, S1.Pin_4
  N7: Компонент1.5V, U1.A, U2.A, U3.A
  N8: U1.E, U2.E, U3.E
  N9: LED1.anode, R1.Pin_1
